# Fritzing sketch trasmitter-receiver-img (saved by Fritzing 0.9.3b)
breadboards: 2

parts:
  Part1 = Arduino Nano (Rev3.0)
  RHT2 = Humidity and Temperature Sensor RHT03 [part_number=DHT22]
  Part2 = NRF24L01+ Breakout Board
  Part3 = Arduino Uno (Rev3) - ICSP
  Part4 = NRF24L01+ Breakout Board

nets:
  N1: Part1.D4, RHT2.Data-signal
  N2: Part1.D7, Part2.CE
  N3: Part1.D8, Part2.CS
  N4: Part1.D11/MOSI, Part2.MOSI
  N5: Part1.D12/MISO, Part2.MISO
  N6: Part1.D13/SCK, Part2.SCK
  N7: Part3.D8, Part4.CS
  N8: Part3.D11_PWM/MOSI, Part4.MOSI
  N9: Part3.D12/MISO, Part4.MISO
  N10: Part3.D13/SCK, Part4.SCK
  GND: Part3.GND, Part4.GND
  N11: Part3.D7, Part4.CE
  3V3: Part3.3V3, Part4.VCC

notes:
  DHT22
